// Logisim project GTP_project_full2.circ as structural Verilog: 14 circuits, main circuit main
module main (
);

  wire _1, _2, _3, _4, _5, _11, _12, _13, _14, _15, _21, _22, _23, _24, _25, busy,
       calculate_input_1_counter_2, calculate_input_1_exit_2, calculate_input_1_parking_2, clock_1_out,
       count_car_1_all_available, count_car_1_full_parking, down, Exit, f, g1_1_out, g2_1_out, g3_1_out,
       g4_1_out, g5_1_out, Input__1_2, Input__2_2, Input__3_2, Input__4_2, Input__5_2, Input__6_2,
       Input__7_2, Input__8_2, Input__9_2, Input_exit_2, Input_parking_2, main_logic_1_busy, n1, n2, n3, n4,
       n5, n6, n7, n8, n9, output_and_display_1__0, output_and_display_1__1_2, output_and_display_1__2_2,
       output_and_display_1__3_2, output_and_display_1__4_2, output_and_display_1_count_button,
       output_and_display_1_exit_2, output_and_display_1_parking_2, output_and_display_1_reset, Parking,
       S1_q, S2_q, S3_q, S4_q, S5_q, select_position__11, select_position__12, select_position__13,
       select_position__14, select_position__15, select_position__21, select_position__22,
       select_position__23, select_position__24, select_position__25, Sf_q, up, usable, where_to_go_1_go_1,
       where_to_go_1_go_2, where_to_go_1_go_3, where_to_go_1_go_4, where_to_go_1_go_5;
  wire [4:0] calculate_input_1_output, Input_b1, Input_b2, Input_b3, Input_b4, Input_b5, Input_b6, Input_b7,
       Input_b8, Input_b9;
  wire [7:0] display1, display2, display_c1, display_c2;

  _7_Segment_Display u_7_segment_display_1 (
    .g(display_c2[3]), .f(display_c2[2]), .a(display_c2[1]), .b(display_c2[0]), .e(display_c2[4]),
    .d(display_c2[5]), .c(display_c2[6]));  // open: dp
  LED led_1 (.in(_15));
  LED led_2 (.in(_14));
  LED led_3 (.in(_13));
  LED led_4 (.in(_12));
  LED led_5 (.in(_11));
  _7_Segment_Display u_7_segment_display_2 (
    .g(display_c1[0]), .f(display_c1[1]), .a(display_c1[2]), .b(display_c1[3]), .e(display_c1[6]),
    .d(display_c1[5]), .c(display_c1[4]));  // open: dp
  LED led_6 (.in(_25));
  LED led_7 (.in(_24));
  LED led_8 (.in(_23));
  LED led_9 (.in(_22));
  LED led_10 (.in(_21));
  LED u__5 (.in(_5));
  LED u__4 (.in(_4));
  LED u__3 (.in(_3));
  LED u__2 (.in(_2));
  LED u__1 (.in(_1));
  LED u_F (.in(f));
  LED u_up (.in(up));
  LED u_down (.in(down));
  LED u_usable (.in(usable));
  LED u_busy (.in(busy));
  _7_Segment_Display u_7_segment_display_3 (
    .g(display2[3]), .f(display2[2]), .a(display2[1]), .b(display2[0]), .e(display2[4]), .d(display2[5]),
    .c(display2[6]));  // open: dp
  Button _7 (.out(n7));
  Button _4_2 (.out(n4));
  Button _1_2 (.out(n1));
  _7_Segment_Display u_7_segment_display_4 (
    .g(display1[0]), .f(display1[1]), .a(display1[2]), .b(display1[3]), .e(display1[6]), .d(display1[5]),
    .c(display1[4]));  // open: dp
  Button _8 (.out(n8));
  Button _5_2 (.out(n5));
  Button _2_2 (.out(n2));
  Button u_exit (.out(Exit));
  Button u_parking (.out(Parking));
  Button _9 (.out(n9));
  Button _6 (.out(n6));
  Button _3_2 (.out(n3));
  Clock clock_1 (.out(clock_1_out));
  D_Flip_Flop Sf (.clk(clock_1_out), .D(f), .Q(Sf_q));  // open: Qn, preset, en, reset
  D_Flip_Flop S1 (.clk(clock_1_out), .D(_1), .Q(S1_q));  // open: Qn, preset, en, reset
  D_Flip_Flop S2 (.clk(clock_1_out), .D(_2), .Q(S2_q));  // open: Qn, preset, en, reset
  D_Flip_Flop S3 (.clk(clock_1_out), .D(_3), .Q(S3_q));  // open: Qn, preset, en, reset
  D_Flip_Flop S4 (.clk(clock_1_out), .D(_4), .Q(S4_q));  // open: Qn, preset, en, reset
  D_Flip_Flop S5 (.clk(clock_1_out), .D(_5), .Q(S5_q));  // open: Qn, preset, en, reset
  g5 g5_1 (.out(g5_1_out), .in(where_to_go_1_go_5));
  g4 g4_1 (.out(g4_1_out), .in(where_to_go_1_go_4));
  g3 g3_1 (.out(g3_1_out), .in(where_to_go_1_go_3));
  g2 g2_1 (.out(g2_1_out), .in(where_to_go_1_go_2));
  g1 g1_1 (.out(g1_1_out), .in(where_to_go_1_go_1));
  count_car count_car_1 (
    .parking(Parking), .exit(Exit), .full_parking(count_car_1_full_parking),
    .all_available(count_car_1_all_available), .d1(display_c1), .d2(display_c2));
  Main_logic main_logic_1 (
    .Sf(Sf_q), .S1(S1_q), .S2(S2_q), .S3(S3_q), .S4(S4_q), .S5(S5_q), .G1(g1_1_out), .G2(g2_1_out),
    .G3(g3_1_out), .G4(g4_1_out), .G5(g5_1_out), .go_Sf(f), .go_s1(_1), .go_s2(_2), .go_s3(_3), .go_s4(_4),
    .go_s5(_5), .busy(main_logic_1_busy), .up(up), .down(down));
  Process_input Input (
    ._1(n1), ._2(n2), ._3(n3), ._4(n4), ._5(n5), ._6(n6), ._7(n7), ._8(n8), ._9(n9), .parking(Parking),
    .exit(Exit), .full_parking(count_car_1_full_parking), .all_available(count_car_1_all_available),
    ._1_2(Input__1_2), .b1(Input_b1), ._2_2(Input__2_2), .b2(Input_b2), ._3_2(Input__3_2), .b3(Input_b3),
    ._4_2(Input__4_2), .b4(Input_b4), ._5_2(Input__5_2), .b5(Input_b5), ._6_2(Input__6_2), .b6(Input_b6),
    ._7_2(Input__7_2), .b7(Input_b7), ._8_2(Input__8_2), .b8(Input_b8), ._9_2(Input__9_2), .b9(Input_b9),
    .Parking_2(Input_parking_2), .Exit_2(Input_exit_2));
  output_and_display output_and_display_1 (
    ._1(Input__1_2), .in_2(Input_b1), ._2(Input__2_2), .in_4(Input_b2), ._3(Input__3_2), .in_6(Input_b3),
    ._4(Input__4_2), .in_8(Input_b4), ._5(Input__5_2), .in_10(Input_b5), ._6(Input__6_2), .in_12(Input_b6),
    ._7(Input__7_2), .in_14(Input_b7), ._8(Input__8_2), .in_16(Input_b8), ._9(Input__9_2), .in_18(Input_b9),
    .parking(Input_parking_2), .exit(Input_exit_2), ._0(output_and_display_1__0),
    ._1_2(output_and_display_1__1_2), ._2_2(output_and_display_1__2_2), ._3_2(output_and_display_1__3_2),
    ._4_2(output_and_display_1__4_2), .d1(display1), .d2(display2),
    .count_button(output_and_display_1_count_button), .reset(output_and_display_1_reset),
    .parking_2(output_and_display_1_parking_2), .exit_2(output_and_display_1_exit_2));
  available available_1 (
    ._11(select_position__11), ._21(select_position__21), ._12(select_position__12),
    ._22(select_position__22), ._13(select_position__13), ._23(select_position__23),
    ._14(select_position__14), ._24(select_position__24), ._15(select_position__15),
    ._25(select_position__25), .parking(calculate_input_1_parking_2), .exit(calculate_input_1_exit_2),
    .counter(calculate_input_1_counter_2), .Reset(busy), ._11_2(_11), ._21_2(_21), ._12_2(_12), ._22_2(_22),
    ._13_2(_13), ._23_2(_23), ._14_2(_14), ._24_2(_24), ._15_2(_15), ._25_2(_25));
  Decoder #(.enable("false")) decoder_1 (.out0(usable), .out1(busy), .sel(main_logic_1_busy));
  calculate_input calculate_input_1 (
    ._0(output_and_display_1__0), ._1(output_and_display_1__1_2), ._2(output_and_display_1__2_2),
    ._3(output_and_display_1__3_2), ._4(output_and_display_1__4_2),
    .counter(output_and_display_1_count_button), .reset(output_and_display_1_reset),
    .parking(output_and_display_1_parking_2), .exit(output_and_display_1_exit_2),
    .\output (calculate_input_1_output), .counter_2(calculate_input_1_counter_2),
    .parking_2(calculate_input_1_parking_2), .exit_2(calculate_input_1_exit_2));
  input_available select_position (
    ._0(calculate_input_1_output), ._11(select_position__11), ._21(select_position__21),
    ._12(select_position__12), ._22(select_position__22), ._13(select_position__13),
    ._23(select_position__23), ._14(select_position__14), ._24(select_position__24),
    ._15(select_position__15), ._25(select_position__25));
  where_to_go where_to_go_1 (
    ._0(calculate_input_1_output), .Go_1(where_to_go_1_go_1), .Go_2(where_to_go_1_go_2),
    .Go_3(where_to_go_1_go_3), .Go_4(where_to_go_1_go_4), .Go_5(where_to_go_1_go_5));

  // Notes on the sheet:
  //   Available
  //   Display Car Counter
  //   Control Panel
  //   Floor
  //   Up - Down
  //   Usable
  //   Display Position
  //   Numpad
  //   Parking - ต้องการทีจะจอดรถ
  //   Exit  - ต้องการนำรถออก
  //   Numpad - ป้อนค่าของ position
  //   มีไฟ - ไม่ว่าง
  //   ไม่มีไฟ - ว่าง
  //   Usable -  สถานะว่าการทำงานของlift 
  //   Floor -  ตำแหน่งของ lift
  //   GTP tower parking
  //   Available - ไฟแสดงว่าตำแหน่งนั้นว่างหรือไม่ว่าง
  //   Display Position - แสดงผลposition ที่ต้องการเลือก 
  //   Position - หลักสิบคือแถว หลักหน่วยคือชั้น
  //   Display Car Counter - แสดงจำนวนที่จอดรถที่ว่าง
  //   Up - Down แสดงสถานะว่าlift กำลังขึ้นหรือลง
  //   การออกแบบ - มี 2 แถว แถวละ5ชั้น สามารถจอดรถสุทธิที่ 10 คัน
  //   1. ดู position จากไฟสถานะ Available
  //   3. ป้อน position ที่ต้องการลงบน Numpad 
  //   การใช้งาน
  //   *ก่อนการใช้งานทุกครั้ง ต้องมีไฟที่สถานะusable
  //   1.1 กรณีต้องการ Parking ต้องเลือกposition ที่ไม่มีไฟ
  //   1.2 กรณีต้องการ Exit ต้องเลือกposition ที่มีไฟ
  //   2. กด Parking หรือ Exit ตามที่ต้องการใช้งาน
  //   รายชื่อสมาชิค
  //   1. นายพิตตินันท์ เลิศสิริมั่นคง 6210612658
  //   2. นายภูชิชย์ กลีบมาลัย 6210612716
  //   3. นายวงศกร กองกะมุด 6310611006
  //   4.นายชนนชนม์ เอมเเสง 6310682759
  //   5. นายธฤษณุ เตชะธัญโชติ 6310682775
endmodule

module Process_input (
  input  _1,
  input  _2,
  input  _3,
  input  _4,
  input  _5,
  input  _6,
  input  _7,
  input  _8,
  input  _9,
  input  parking,
  input  exit,
  input  full_parking,
  input  all_available,
  output _1_2,
  output [4:0] b1,
  output _2_2,
  output [4:0] b2,
  output _3_2,
  output [4:0] b3,
  output _4_2,
  output [4:0] b4,
  output _5_2,
  output [4:0] b5,
  output _6_2,
  output [4:0] b6,
  output _7_2,
  output [4:0] b7,
  output _8_2,
  output [4:0] b8,
  output _9_2,
  output [4:0] b9,
  output Parking_2,
  output Exit_2
);

  wire clock_1_out, multiplexer_1_out, multiplexer_2_out, multiplexer_3_out, multiplexer_4_out,
       multiplexer_5_out, multiplexer_6_out, multiplexer_7_out, multiplexer_8_out, multiplexer_9_out,
       multiplexer_10_out, multiplexer_11_out, or_1_out, register_1_q;

  Multiplexer multiplexer_1 (.in0(1'b0), .in1(1'b1), .out(multiplexer_1_out), .sel(exit), .en(all_available));
  Multiplexer multiplexer_2 (.in0(1'b0), .in1(1'b1), .out(multiplexer_2_out), .sel(parking), .en(full_parking));
  Multiplexer multiplexer_3 (.in1(_1), .out(multiplexer_3_out), .sel(register_1_q), .en(register_1_q));  // open: in0
  Multiplexer multiplexer_4 (.in1(_2), .out(multiplexer_4_out), .sel(register_1_q), .en(register_1_q));  // open: in0
  Multiplexer multiplexer_5 (.in1(_3), .out(multiplexer_5_out), .sel(register_1_q), .en(register_1_q));  // open: in0
  Multiplexer multiplexer_6 (.in1(_4), .out(multiplexer_6_out), .sel(register_1_q), .en(register_1_q));  // open: in0
  Multiplexer multiplexer_7 (.in1(_5), .out(multiplexer_7_out), .sel(register_1_q), .en(register_1_q));  // open: in0
  Multiplexer multiplexer_8 (.in1(_6), .out(multiplexer_8_out), .sel(register_1_q), .en(register_1_q));  // open: in0
  Multiplexer multiplexer_9 (.in1(_7), .out(multiplexer_9_out), .sel(register_1_q), .en(register_1_q));  // open: in0
  Multiplexer multiplexer_10 (.in1(_8), .out(multiplexer_10_out), .sel(register_1_q), .en(register_1_q));  // open: in0
  Multiplexer multiplexer_11 (.in1(_9), .out(multiplexer_11_out), .sel(register_1_q), .en(register_1_q));  // open: in0
  or or_1 (or_1_out, multiplexer_1_out, multiplexer_2_out);
  Multiplexer #(.width(5), .enable("false")) multiplexer_12 (
    .in1(5'b00001), .out(b1), .sel(multiplexer_3_out));  // open: in0
  Multiplexer #(.width(5), .enable("false")) multiplexer_13 (
    .in1(5'b00010), .out(b2), .sel(multiplexer_4_out));  // open: in0
  Multiplexer #(.width(5), .enable("false")) multiplexer_14 (
    .in1(5'b00011), .out(b3), .sel(multiplexer_5_out));  // open: in0
  Multiplexer #(.width(5), .enable("false")) multiplexer_15 (
    .in1(5'b00100), .out(b4), .sel(multiplexer_6_out));  // open: in0
  Multiplexer #(.width(5), .enable("false")) multiplexer_16 (
    .in1(5'b00101), .out(b5), .sel(multiplexer_7_out));  // open: in0
  Multiplexer #(.width(5), .enable("false")) multiplexer_17 (
    .in1(5'b00110), .out(b6), .sel(multiplexer_8_out));  // open: in0
  Multiplexer #(.width(5), .enable("false")) multiplexer_18 (
    .in1(5'b00111), .out(b7), .sel(multiplexer_9_out));  // open: in0
  Multiplexer #(.width(5), .enable("false")) multiplexer_19 (
    .in1(5'b01000), .out(b8), .sel(multiplexer_10_out));  // open: in0
  Multiplexer #(.width(5), .enable("false")) multiplexer_20 (
    .in1(5'b01001), .out(b9), .sel(multiplexer_11_out));  // open: in0
  Register #(.width(1), .trigger("high")) register_1 (.D(or_1_out), .Q(register_1_q), .clk(or_1_out));  // open: en, clr
  D_Flip_Flop d_ff_1 (.Q(_1_2), .preset(multiplexer_3_out), .reset(clock_1_out));  // open: clk, D, Qn, en
  D_Flip_Flop d_ff_2 (.Q(_2_2), .preset(multiplexer_4_out), .reset(clock_1_out));  // open: clk, D, Qn, en
  D_Flip_Flop d_ff_3 (.Q(_3_2), .preset(multiplexer_5_out), .reset(clock_1_out));  // open: clk, D, Qn, en
  D_Flip_Flop d_ff_4 (.Q(_4_2), .preset(multiplexer_6_out), .reset(clock_1_out));  // open: clk, D, Qn, en
  D_Flip_Flop d_ff_5 (.Q(_5_2), .preset(multiplexer_7_out), .reset(clock_1_out));  // open: clk, D, Qn, en
  D_Flip_Flop d_ff_6 (.Q(_6_2), .preset(multiplexer_8_out), .reset(clock_1_out));  // open: clk, D, Qn, en
  D_Flip_Flop d_ff_7 (.Q(_7_2), .preset(multiplexer_9_out), .reset(clock_1_out));  // open: clk, D, Qn, en
  D_Flip_Flop d_ff_8 (.Q(_8_2), .preset(multiplexer_10_out), .reset(clock_1_out));  // open: clk, D, Qn, en
  D_Flip_Flop d_ff_9 (.Q(_9_2), .preset(multiplexer_11_out), .reset(clock_1_out));  // open: clk, D, Qn, en
  D_Flip_Flop d_ff_10 (.Q(Parking_2), .preset(multiplexer_2_out), .reset(clock_1_out));  // open: clk, D, Qn, en
  D_Flip_Flop d_ff_11 (.Q(Exit_2), .preset(multiplexer_1_out), .reset(clock_1_out));  // open: clk, D, Qn, en
  Clock clock_1 (.out(clock_1_out));
endmodule

// display
module output_and_display (
  input  _1,
  input  [4:0] in_2,
  input  _2,
  input  [4:0] in_4,
  input  _3,
  input  [4:0] in_6,
  input  _4,
  input  [4:0] in_8,
  input  _5,
  input  [4:0] in_10,
  input  _6,
  input  [4:0] in_12,
  input  _7,
  input  [4:0] in_14,
  input  _8,
  input  [4:0] in_16,
  input  _9,
  input  [4:0] in_18,
  input  parking,
  input  exit,
  output _0,
  output _1_2,
  output _2_2,
  output _3_2,
  output _4_2,
  output [7:0] d1,
  output [7:0] d2,
  output count_button,
  output reset,
  output parking_2,
  output exit_2
);

  wire clock_1_out, counter_mux_carry, counter_reg_carry;
  wire [4:0] multiplexer_1_out, multiplexer_10_out, multiplexer_11_out, multiplexer_12_out,
       multiplexer_13_out, register_first_index_q;

  Multiplexer #(.width(5), .enable("false")) multiplexer_1 (
    .in1(in_2), .out(multiplexer_1_out), .sel(_1));  // open: in0
  Multiplexer #(.width(5), .enable("false")) multiplexer_2 (
    .in1(in_4), .out(multiplexer_1_out), .sel(_2));  // open: in0
  Multiplexer #(.width(5), .enable("false")) multiplexer_3 (
    .in1(in_6), .out(multiplexer_1_out), .sel(_3));  // open: in0
  Multiplexer #(.width(5), .enable("false")) multiplexer_4 (
    .in1(in_8), .out(multiplexer_1_out), .sel(_4));  // open: in0
  Multiplexer #(.width(5), .enable("false")) multiplexer_5 (
    .in1(in_10), .out(multiplexer_1_out), .sel(_5));  // open: in0
  Multiplexer #(.width(5), .enable("false")) multiplexer_6 (
    .in1(in_12), .out(multiplexer_1_out), .sel(_6));  // open: in0
  Multiplexer #(.width(5), .enable("false")) multiplexer_7 (
    .in1(in_14), .out(multiplexer_1_out), .sel(_7));  // open: in0
  Multiplexer #(.width(5), .enable("false")) multiplexer_8 (
    .in1(in_16), .out(multiplexer_1_out), .sel(_8));  // open: in0
  Multiplexer #(.width(5), .enable("false")) multiplexer_9 (
    .in1(in_18), .out(multiplexer_1_out), .sel(_9));  // open: in0
  or or_1 (reset, parking, exit);
  or or_2 (count_button, _1, _2, _3, _4, _5, _6, _7, _8, _9);
  Counter #(.max('h1)) counter_reg (.carry(counter_reg_carry), .clk(count_button));  // open: load, D, count, Q, clr
  Register #(.width(5)) register_first_index (
    .D(multiplexer_1_out), .en(1'b1), .Q(register_first_index_q), .clk(counter_reg_carry), .clr(reset));
  Counter #(.max('h2)) counter_mux (
    .carry(counter_mux_carry), .clk(count_button), .clr(reset));  // open: load, D, count, Q
  Multiplexer #(.width(5)) multiplexer_10 (
    .in0({5{1'b0}}), .in1(multiplexer_1_out), .out(multiplexer_10_out), .sel(count_button), .en(count_button));
  Multiplexer #(.width(5)) multiplexer_11 (
    .in0({5{1'b0}}), .in1(register_first_index_q), .out(multiplexer_11_out), .sel(counter_mux_carry),
    .en(counter_mux_carry));
  Multiplexer #(.width(5), .enable("false")) multiplexer_12 (
    .in0(multiplexer_10_out), .in1({5{1'b0}}), .out(multiplexer_12_out), .sel(reset));
  Multiplexer #(.width(5), .enable("false")) multiplexer_13 (
    .in0(multiplexer_11_out), .in1({5{1'b0}}), .out(multiplexer_13_out), .sel(reset));
  ROM #(.addrWidth(5)) rom_1 (.addr(multiplexer_12_out), .data(d1));  // open: sel
  ROM #(.addrWidth(5)) rom_2 (.addr(multiplexer_13_out), .data(d2));  // open: sel
  D_Flip_Flop d_ff_1 (.Q(_0), .preset(multiplexer_1_out[0]), .reset(clock_1_out));  // open: clk, D, Qn, en
  D_Flip_Flop d_ff_2 (.Q(_1_2), .preset(multiplexer_1_out[1]), .reset(clock_1_out));  // open: clk, D, Qn, en
  D_Flip_Flop d_ff_3 (.Q(_2_2), .preset(multiplexer_1_out[2]), .reset(clock_1_out));  // open: clk, D, Qn, en
  D_Flip_Flop d_ff_4 (.Q(_3_2), .preset(multiplexer_1_out[3]), .reset(clock_1_out));  // open: clk, D, Qn, en
  D_Flip_Flop d_ff_5 (.Q(_4_2), .preset(multiplexer_1_out[4]), .reset(clock_1_out));  // open: clk, D, Qn, en
  Clock clock_1 (.out(clock_1_out));

  assign exit_2 = exit;
  assign parking_2 = parking;

  // Notes on the sheet:
  //   contents of rom_1 (hex, n*v repeats v):
  //   fe 18 ed 3d 1b 37 77 1c ff 3f
  //   contents of rom_2 (hex, n*v repeats v):
  //   f7 41 3b 6b 4d ee fe c3 ff ef
endmodule

module calculate_input (
  input  _0,
  input  _1,
  input  _2,
  input  _3,
  input  _4,
  input  counter,
  input  reset,
  input  parking,
  input  exit,
  output [4:0] \output ,
  output counter_2,
  output parking_2,
  output exit_2
);

  wire counter_1_carry, counter_2_carry;
  wire [4:0] adder_1_out, multiplexer_1_out, multiplier_1_out, register_1_q, Register_first_index_q;

  Counter #(.max('h1)) counter_1 (.carry(counter_1_carry), .clk(counter), .clr(reset));  // open: load, D, count, Q
  Register #(.width(5)) Register_first_index (
    .D({_4, _3, _2, _1, _0}), .en(1'b1), .Q(Register_first_index_q), .clk(counter_1_carry), .clr(reset));
  Counter #(.max('h2)) u_counter_2 (.carry(counter_2_carry), .clk(counter), .clr(reset));  // open: load, D, count, Q
  Multiplier #(.width(5)) multiplier_1 (
    .a(5'b01010), .b(Register_first_index_q), .out(multiplier_1_out));  // open: cin, cout
  Register #(.width(5), .trigger("high")) register_1 (
    .D(adder_1_out), .Q(register_1_q), .clk(counter_2_carry), .clr(reset));  // open: en
  Adder #(.width(5)) adder_1 (.a({_4, _3, _2, _1, _0}), .b(multiplier_1_out), .out(adder_1_out));  // open: cin, cout
  Multiplexer #(.width(5)) multiplexer_1 (
    .in1(register_1_q), .out(multiplexer_1_out), .sel(counter_2_carry), .en(counter_2_carry));  // open: in0
  Register #(.width(5), .trigger("high")) register_2 (
    .D(multiplexer_1_out), .Q(\output ), .clk(counter_2_carry), .clr(reset));  // open: en

  assign counter_2 = counter;
  assign exit_2 = exit;
  assign parking_2 = parking;
endmodule

module where_to_go (
  input  [4:0] _0,
  output Go_1,
  output Go_2,
  output Go_3,
  output Go_4,
  output Go_5
);

  wire comparator_1_eq, comparator_2_eq, comparator_3_eq, comparator_4_eq, comparator_5_eq, comparator_6_eq,
       comparator_7_eq, comparator_8_eq, comparator_9_eq, comparator_10_eq;

  Comparator #(.width(5)) comparator_1 (.a(5'b01011), .b(_0), .eq(comparator_1_eq));  // open: gt, lt
  Comparator #(.width(5)) comparator_2 (.a(5'b10101), .b(_0), .eq(comparator_2_eq));  // open: gt, lt
  Comparator #(.width(5)) comparator_3 (.a(5'b01100), .b(_0), .eq(comparator_3_eq));  // open: gt, lt
  Comparator #(.width(5)) comparator_4 (.a(5'b10110), .b(_0), .eq(comparator_4_eq));  // open: gt, lt
  Comparator #(.width(5)) comparator_5 (.a(5'b01101), .b(_0), .eq(comparator_5_eq));  // open: gt, lt
  Comparator #(.width(5)) comparator_6 (.a(5'b10111), .b(_0), .eq(comparator_6_eq));  // open: gt, lt
  Comparator #(.width(5)) comparator_7 (.a(5'b01110), .b(_0), .eq(comparator_7_eq));  // open: gt, lt
  Comparator #(.width(5)) comparator_8 (.a(5'b11000), .b(_0), .eq(comparator_8_eq));  // open: gt, lt
  Comparator #(.width(5)) comparator_9 (.a(5'b01111), .b(_0), .eq(comparator_9_eq));  // open: gt, lt
  Comparator #(.width(5)) comparator_10 (.a(5'b11001), .b(_0), .eq(comparator_10_eq));  // open: gt, lt
  or or_1 (Go_1, comparator_1_eq, comparator_2_eq);
  or or_2 (Go_2, comparator_3_eq, comparator_4_eq);
  or or_3 (Go_3, comparator_5_eq, comparator_6_eq);
  or or_4 (Go_4, comparator_7_eq, comparator_8_eq);
  or or_5 (Go_5, comparator_9_eq, comparator_10_eq);
endmodule

module Main_logic (
  input  Sf,
  input  S1,
  input  S2,
  input  S3,
  input  S4,
  input  S5,
  input  G1,
  input  G2,
  input  G3,
  input  G4,
  input  G5,
  output go_Sf,
  output go_s1,
  output go_s2,
  output go_s3,
  output go_s4,
  output go_s5,
  output busy,
  output up,
  output down
);

  wire _1_TO_2_out, _1_TO_3_out, _1_TO_4_out, _1_TO_5_out, _1_TO_F_out, _2_TO_1_out, _2_TO_3_out,
       _2_TO_4_out, _2_TO_5_out, _3_TO_2_out, _3_TO_4_out, _3_TO_5_out, _4_TO_3_out, _5_TO_4_out, F_TO_1_out,
       F_TO_2_out, F_TO_3_out, F_TO_4_out, F_TO_5_out, F_TO_F_out, not_1_out, not_2_out, not_3_out,
       not_4_out, not_5_out, not_6_out, not_7_out, not_8_out, not_9_out, not_10_out, not_11_out, not_12_out,
       not_13_out, not_14_out, not_15_out, or_3_out, or_5_out, or_7_out, or_9_out, UNAVAILABLE_out;

  not not_1 (not_1_out, S1);
  not not_2 (not_2_out, S2);
  not not_3 (not_3_out, S3);
  not not_4 (not_4_out, S4);
  not not_5 (not_5_out, S5);
  not not_6 (not_6_out, G1);
  not not_7 (not_7_out, G2);
  not not_8 (not_8_out, G3);
  not not_9 (not_9_out, G4);
  not not_10 (not_10_out, G5);
  not not_11 (not_11_out, G1);
  not not_12 (not_12_out, G2);
  not not_13 (not_13_out, G3);
  not not_14 (not_14_out, G4);
  not not_15 (not_15_out, G5);
  and F_TO_F (F_TO_F_out, not_1_out, not_2_out, not_3_out, not_4_out, not_5_out, not_6_out, not_7_out, not_8_out, not_9_out, not_10_out);
  and F_TO_1 (F_TO_1_out, Sf, G1);
  and F_TO_2 (F_TO_2_out, Sf, G2);
  and F_TO_3 (F_TO_3_out, Sf, G3);
  and F_TO_4 (F_TO_4_out, Sf, G4);
  and F_TO_5 (F_TO_5_out, Sf, G5);
  and _1_TO_2 (_1_TO_2_out, S1, G2);
  and _1_TO_3 (_1_TO_3_out, S1, G3);
  and _1_TO_4 (_1_TO_4_out, S1, G4);
  and _1_TO_5 (_1_TO_5_out, S1, G5);
  and _2_TO_3 (_2_TO_3_out, S2, G3);
  and _2_TO_4 (_2_TO_4_out, S2, G4);
  and _2_TO_5 (_2_TO_5_out, S2, G5);
  and _3_TO_4 (_3_TO_4_out, S3, G4);
  and _3_TO_5 (_3_TO_5_out, S3, G5);
  and _4_TO_5 (go_s5, S4, G5);
  and UNAVAILABLE (UNAVAILABLE_out, not_11_out, not_12_out, not_13_out, not_14_out, not_15_out);
  and _5_TO_4 (_5_TO_4_out, UNAVAILABLE_out, S5);
  and _4_TO_3 (_4_TO_3_out, UNAVAILABLE_out, S4);
  and _3_TO_2 (_3_TO_2_out, UNAVAILABLE_out, S3);
  and _2_TO_1 (_2_TO_1_out, UNAVAILABLE_out, S2);
  and _1_TO_F (_1_TO_F_out, UNAVAILABLE_out, S1);
  or or_1 (go_Sf, F_TO_F_out, _1_TO_F_out);
  or or_2 (go_s1, F_TO_1_out, F_TO_2_out, F_TO_3_out, F_TO_4_out, F_TO_5_out, _2_TO_1_out);
  or or_3 (or_3_out, F_TO_1_out, F_TO_2_out, F_TO_3_out, F_TO_4_out, F_TO_5_out);
  or or_4 (go_s2, _1_TO_2_out, _1_TO_3_out, _3_TO_2_out, _1_TO_4_out, _1_TO_5_out);
  or or_5 (or_5_out, _1_TO_2_out, _1_TO_3_out, _1_TO_4_out, _1_TO_5_out);
  or or_6 (go_s3, _2_TO_3_out, _2_TO_4_out, _4_TO_3_out, _2_TO_5_out);
  or or_7 (or_7_out, _2_TO_3_out, _2_TO_4_out, _2_TO_5_out);
  or or_8 (go_s4, _3_TO_4_out, _5_TO_4_out, _3_TO_5_out);
  or or_9 (or_9_out, _3_TO_4_out, _3_TO_5_out);
  or or_10 (busy, G1, G2, G3, G4, G5, _5_TO_4_out, _4_TO_3_out, _3_TO_2_out, _2_TO_1_out, _1_TO_F_out);
  or or_11 (up, or_3_out, or_5_out, or_7_out, or_9_out, go_s5);
  or or_12 (down, _5_TO_4_out, _4_TO_3_out, _3_TO_2_out, _2_TO_1_out, _1_TO_F_out);
endmodule

// G5
module g5 (
  input  in,
  output out
);

  wire clock_1_out, d_ff_1_q, d_ff_2_q, d_ff_3_q, d_ff_4_q, d_ff_5_q;

  Clock clock_1 (.out(clock_1_out));
  D_Flip_Flop d_ff_1 (.clk(clock_1_out), .D(d_ff_2_q), .Q(d_ff_1_q));  // open: Qn, preset, en, reset
  D_Flip_Flop d_ff_2 (.clk(clock_1_out), .D(d_ff_3_q), .Q(d_ff_2_q));  // open: Qn, preset, en, reset
  D_Flip_Flop d_ff_3 (.clk(clock_1_out), .D(d_ff_4_q), .Q(d_ff_3_q));  // open: Qn, preset, en, reset
  D_Flip_Flop d_ff_4 (.clk(clock_1_out), .D(d_ff_5_q), .Q(d_ff_4_q));  // open: Qn, preset, en, reset
  D_Flip_Flop d_ff_5 (.clk(clock_1_out), .D(in), .Q(d_ff_5_q));  // open: Qn, preset, en, reset
  or or_1 (out, d_ff_1_q, d_ff_2_q, d_ff_3_q, d_ff_4_q, d_ff_5_q);
endmodule

// G4
module g4 (
  input  in,
  output out
);

  wire clock_1_out, d_ff_1_q, d_ff_2_q, d_ff_3_q, d_ff_4_q;

  Clock clock_1 (.out(clock_1_out));
  D_Flip_Flop d_ff_1 (.clk(clock_1_out), .D(d_ff_2_q), .Q(d_ff_1_q));  // open: Qn, preset, en, reset
  D_Flip_Flop d_ff_2 (.clk(clock_1_out), .D(d_ff_3_q), .Q(d_ff_2_q));  // open: Qn, preset, en, reset
  D_Flip_Flop d_ff_3 (.clk(clock_1_out), .D(d_ff_4_q), .Q(d_ff_3_q));  // open: Qn, preset, en, reset
  D_Flip_Flop d_ff_4 (.clk(clock_1_out), .D(in), .Q(d_ff_4_q));  // open: Qn, preset, en, reset
  or or_1 (out, d_ff_1_q, d_ff_2_q, d_ff_3_q, d_ff_4_q);
endmodule

// G3
module g3 (
  input  in,
  output out
);

  wire clock_1_out, d_ff_1_q, d_ff_2_q, d_ff_3_q;

  Clock clock_1 (.out(clock_1_out));
  D_Flip_Flop d_ff_1 (.clk(clock_1_out), .D(d_ff_2_q), .Q(d_ff_1_q));  // open: Qn, preset, en, reset
  D_Flip_Flop d_ff_2 (.clk(clock_1_out), .D(d_ff_3_q), .Q(d_ff_2_q));  // open: Qn, preset, en, reset
  D_Flip_Flop d_ff_3 (.clk(clock_1_out), .D(in), .Q(d_ff_3_q));  // open: Qn, preset, en, reset
  or or_1 (out, d_ff_1_q, d_ff_2_q, d_ff_3_q);
endmodule

// G2
module g2 (
  input  in,
  output out
);

  wire clock_1_out, d_ff_1_q, d_ff_2_q;

  Clock clock_1 (.out(clock_1_out));
  D_Flip_Flop d_ff_1 (.clk(clock_1_out), .D(d_ff_2_q), .Q(d_ff_1_q));  // open: Qn, preset, en, reset
  D_Flip_Flop d_ff_2 (.clk(clock_1_out), .D(in), .Q(d_ff_2_q));  // open: Qn, preset, en, reset
  or or_1 (out, d_ff_1_q, d_ff_2_q);
endmodule

// G1
module g1 (
  input  in,
  output out
);

  wire clock_1_out;

  Clock clock_1 (.out(clock_1_out));
  D_Flip_Flop d_ff_1 (.clk(clock_1_out), .D(in), .Q(out));  // open: Qn, preset, en, reset
endmodule

module count_car (
  input  parking,
  input  exit,
  output full_parking,
  output all_available,
  output [7:0] d1,
  output [7:0] d2
);

  wire comparator_1_eq, comparator_2_eq, comparator_3_eq, comparator_4_eq, multiplexer_1_out,
       multiplexer_2_out, or_1_out;
  wire [4:0] counter_1_q;

  Multiplexer #(.enable("false")) multiplexer_1 (
    .in0(parking), .in1(1'b0), .out(multiplexer_1_out), .sel(comparator_3_eq));
  Multiplexer #(.enable("false")) multiplexer_2 (
    .in0(exit), .in1(1'b0), .out(multiplexer_2_out), .sel(comparator_4_eq));
  or or_1 (or_1_out, multiplexer_1_out, multiplexer_2_out);
  Counter #(.width(5), .max('ha)) counter_1 (
    .load(multiplexer_1_out), .count(1'b1), .Q(counter_1_q), .clk(or_1_out));  // open: D, carry, clr
  Comparator #(.width(5)) comparator_1 (.a(5'b00001), .b(counter_1_q), .eq(comparator_1_eq));  // open: gt, lt
  Comparator #(.width(5)) comparator_2 (.a({5{1'b0}}), .b(counter_1_q), .eq(comparator_2_eq));  // open: gt, lt
  ROM #(.addrWidth(5)) rom_1 (.addr(counter_1_q), .data(d1));  // open: sel
  ROM #(.addrWidth(5)) rom_2 (.addr(counter_1_q), .data(d2));  // open: sel
  Comparator #(.width(5)) comparator_3 (.a(counter_1_q), .b(5'b00001), .eq(comparator_3_eq));  // open: gt, lt
  Comparator #(.width(5)) comparator_4 (.a(counter_1_q), .b({5{1'b0}}), .eq(comparator_4_eq));  // open: gt, lt
  not not_1 (full_parking, comparator_1_eq);
  not not_2 (all_available, comparator_2_eq);
  _7_Segment_Display u_7_segment_display_1 (
    .g(d2[3]), .f(d2[2]), .a(d2[1]), .b(d2[0]), .e(d2[4]), .d(d2[5]), .c(d2[6]));  // open: dp
  _7_Segment_Display u_7_segment_display_2 (
    .g(d1[0]), .f(d1[1]), .a(d1[2]), .b(d1[3]), .e(d1[6]), .d(d1[5]), .c(d1[4]));  // open: dp

  // Notes on the sheet:
  //   contents of rom_1 (hex, n*v repeats v):
  //   fe 7e 18 ed 3d 1b 37 77 1c ff 3f fe 18 ed 3d 1b 37 77 1c ff 3f
  //   contents of rom_2 (hex, n*v repeats v):
  //   41 77 9*f7 10*41
endmodule

module available (
  input  _11,
  input  _21,
  input  _12,
  input  _22,
  input  _13,
  input  _23,
  input  _14,
  input  _24,
  input  _15,
  input  _25,
  input  parking,
  input  exit,
  input  counter,
  input  Reset,
  output _11_2,
  output _21_2,
  output _12_2,
  output _22_2,
  output _13_2,
  output _23_2,
  output _14_2,
  output _24_2,
  output _15_2,
  output _25_2
);

  wire counter_1_carry, multiplexer_1_out, multiplexer_2_out, multiplexer_3_out, multiplexer_4_out,
       multiplexer_5_out, multiplexer_6_out, multiplexer_7_out, multiplexer_8_out, multiplexer_9_out,
       multiplexer_10_out, register_1_q, register_2_q, register_3_q, register_4_q, register_5_q,
       register_6_q, register_7_q, register_8_q, register_9_q, register_10_q, register_11_q;

  Register #(.width(1)) register_1 (.D(parking), .Q(register_1_q), .clk(parking), .clr(Reset));  // open: en
  Counter #(.max('h2)) counter_1 (.carry(counter_1_carry), .clk(counter), .clr(Reset));  // open: load, D, count, Q
  Register #(.width(1)) register_2 (.D(_11), .Q(register_2_q), .clk(_11), .clr(Reset));  // open: en
  Register #(.width(1)) register_3 (.D(_21), .Q(register_3_q), .clk(_21), .clr(Reset));  // open: en
  Register #(.width(1)) register_4 (.D(_12), .Q(register_4_q), .clk(_12), .clr(Reset));  // open: en
  Register #(.width(1)) register_5 (.D(_22), .Q(register_5_q), .clk(_22), .clr(Reset));  // open: en
  Register #(.width(1)) register_6 (.D(_13), .Q(register_6_q), .clk(_13), .clr(Reset));  // open: en
  Register #(.width(1)) register_7 (.D(_23), .Q(register_7_q), .clk(_23), .clr(Reset));  // open: en
  Register #(.width(1)) register_8 (.D(_14), .Q(register_8_q), .clk(_14), .clr(Reset));  // open: en
  Register #(.width(1)) register_9 (.D(_24), .Q(register_9_q), .clk(_24), .clr(Reset));  // open: en
  Register #(.width(1)) register_10 (.D(_15), .Q(register_10_q), .clk(_15), .clr(Reset));  // open: en
  Register #(.width(1)) register_11 (.D(_25), .Q(register_11_q), .clk(_25), .clr(Reset));  // open: en
  Multiplexer multiplexer_1 (.in0(1'b0), .in1(1'b1), .out(multiplexer_1_out), .sel(register_1_q), .en(register_2_q));
  Multiplexer multiplexer_2 (.in0(1'b0), .in1(1'b1), .out(multiplexer_2_out), .sel(register_1_q), .en(register_3_q));
  Multiplexer multiplexer_3 (.in0(1'b0), .in1(1'b1), .out(multiplexer_3_out), .sel(register_1_q), .en(register_4_q));
  Multiplexer multiplexer_4 (.in0(1'b0), .in1(1'b1), .out(multiplexer_4_out), .sel(register_1_q), .en(register_5_q));
  Multiplexer multiplexer_5 (.in0(1'b0), .in1(1'b1), .out(multiplexer_5_out), .sel(register_1_q), .en(register_6_q));
  Multiplexer multiplexer_6 (.in0(1'b0), .in1(1'b1), .out(multiplexer_6_out), .sel(register_1_q), .en(register_7_q));
  Multiplexer multiplexer_7 (.in0(1'b0), .in1(1'b1), .out(multiplexer_7_out), .sel(register_1_q), .en(register_8_q));
  Multiplexer multiplexer_8 (.in0(1'b0), .in1(1'b1), .out(multiplexer_8_out), .sel(register_1_q), .en(register_9_q));
  Multiplexer multiplexer_9 (.in0(1'b0), .in1(1'b1), .out(multiplexer_9_out), .sel(register_1_q), .en(register_10_q));
  Multiplexer multiplexer_10 (.in0(1'b0), .in1(1'b1), .out(multiplexer_10_out), .sel(register_1_q), .en(register_11_q));
  Register #(.width(1), .trigger("high")) register_12 (
    .D(multiplexer_1_out), .Q(_11_2), .clk(counter_1_carry));  // open: en, clr
  Register #(.width(1), .trigger("high")) register_13 (
    .D(multiplexer_2_out), .Q(_21_2), .clk(counter_1_carry));  // open: en, clr
  Register #(.width(1), .trigger("high")) register_14 (
    .D(multiplexer_3_out), .Q(_12_2), .clk(counter_1_carry));  // open: en, clr
  Register #(.width(1), .trigger("high")) register_15 (
    .D(multiplexer_4_out), .Q(_22_2), .clk(counter_1_carry));  // open: en, clr
  Register #(.width(1), .trigger("high")) register_16 (
    .D(multiplexer_5_out), .Q(_13_2), .clk(counter_1_carry));  // open: en, clr
  Register #(.width(1), .trigger("high")) register_17 (
    .D(multiplexer_6_out), .Q(_23_2), .clk(counter_1_carry));  // open: en, clr
  Register #(.width(1), .trigger("high")) register_18 (
    .D(multiplexer_7_out), .Q(_14_2), .clk(counter_1_carry));  // open: en, clr
  Register #(.width(1), .trigger("high")) register_19 (
    .D(multiplexer_8_out), .Q(_24_2), .clk(counter_1_carry));  // open: en, clr
  Register #(.width(1), .trigger("high")) register_20 (
    .D(multiplexer_9_out), .Q(_15_2), .clk(counter_1_carry));  // open: en, clr
  Register #(.width(1), .trigger("high")) register_21 (
    .D(multiplexer_10_out), .Q(_25_2), .clk(counter_1_carry));  // open: en, clr
endmodule

module input_available (
  input  [4:0] _0,
  output _11,
  output _21,
  output _12,
  output _22,
  output _13,
  output _23,
  output _14,
  output _24,
  output _15,
  output _25
);

  Comparator #(.width(5)) comparator_1 (.a(5'b01011), .b(_0), .eq(_11));  // open: gt, lt
  Comparator #(.width(5)) comparator_2 (.a(5'b10101), .b(_0), .eq(_21));  // open: gt, lt
  Comparator #(.width(5)) comparator_3 (.a(5'b01100), .b(_0), .eq(_12));  // open: gt, lt
  Comparator #(.width(5)) comparator_4 (.a(5'b10110), .b(_0), .eq(_22));  // open: gt, lt
  Comparator #(.width(5)) comparator_5 (.a(5'b01101), .b(_0), .eq(_13));  // open: gt, lt
  Comparator #(.width(5)) comparator_6 (.a(5'b10111), .b(_0), .eq(_23));  // open: gt, lt
  Comparator #(.width(5)) comparator_7 (.a(5'b01110), .b(_0), .eq(_14));  // open: gt, lt
  Comparator #(.width(5)) comparator_8 (.a(5'b11000), .b(_0), .eq(_24));  // open: gt, lt
  Comparator #(.width(5)) comparator_9 (.a(5'b01111), .b(_0), .eq(_15));  // open: gt, lt
  Comparator #(.width(5)) comparator_10 (.a(5'b11001), .b(_0), .eq(_25));  // open: gt, lt
endmodule
